# Fritzing sketch ArduinoNano_ESP8266_DHT11-Sensor_NokiaLCD (saved by Fritzing 0.9.2b)
breadboards: 2

parts:
  DHT1 = DHT11 Humitidy and Temperature Sensor
  IC1 = '4050 Hex Buffer
  Part1 = Arduino Nano (Rev3.0) (ICSP)
  U1 = ESP8266 WiFi Module [part_number=ESP8266]
  USB1 = USB connector [package=THT]
  IC2 = '4050 Hex Buffer
  Nokia_5110_LCD_Module1 = Nokia5110LCDModule
  R1 = Trimmer Potentiometer [maximum_resistance=10kΩ package=THT]

nets:
  VCC: DHT1.VDD, U1.VCC, USB1.d+, Nokia_5110_LCD_Module1.Vcc, R1.leg1
  N1: DHT1.DATA, Part1.D10
  GND: DHT1.GND, IC1.VSS, Part1.GND, USB1.d-, IC2.VSS, Nokia_5110_LCD_Module1.Grnd, R1.leg2
  VCC_2: IC1.VCC, Part1.5V
  N2: IC1.D, Part1.D4
  N3: IC1.J, U1.CH_PD
  N4: IC1.F, Part1.D2
  N5: IC1.L, U1.RXD
  N6: Part1.D3, U1.TXD
  N7: Part1.D5, IC2.A
  N8: Part1.D6, IC2.B
  N9: Part1.D7, IC2.C
  N10: IC2.G, Nokia_5110_LCD_Module1.D/C
  N11: IC2.H, Nokia_5110_LCD_Module1.SCE
  N12: IC2.I, Nokia_5110_LCD_Module1.RST
  N13: Nokia_5110_LCD_Module1.LED, R1.wiper

notes:
  USB power source (3.3V) powers the ESP8266 and the DHT11 sensor
  Arduino power source (5V) powers the 4050 level shifter chip

custom parts:
  DHT11 Humitidy and Temperature Sensor: DHT11 Humidity and Temperature Sensor
  ESP8266 WiFi Module: Generic WiFi Module based on the ESP8266 with onboard PCB antenna and UART communications
  : Nokia 5110 LCD with 8 pin. It's a 45mm*45mm module part. Description: The Nokia 5110 is a basic graphic LCD screen for lots of applications. It was originally intended for as a cell phone screen. This one is mounted on an easy to solder PCB. It uses the PCD8544 controller. The PCD8544 is a low power CMOS LCD controller/driver, designed to drive a graphic display of 48 rows and 84 columns. All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
